# Fritzing sketch scheme (saved by Fritzing 0.6.4b)

parts:
  Freq_2 = Rotary Potentiometer (Small) [maximum_resistance=5kΩ]
  Decay_2 = Rotary Potentiometer (Small) [maximum_resistance=5kΩ]
  Freq_1 = Rotary Potentiometer (Small) [maximum_resistance=5kΩ]
  Decay_1 = Rotary Potentiometer (Small) [maximum_resistance=5kΩ]
  Freq = Rotary Potentiometer (Small) [maximum_resistance=5kΩ]
  Beat_freq = Rotary Potentiometer (Small) [maximum_resistance=5kΩ]
  Mute = Pushbutton [package="[THT]"]
  Rythm = Pushbutton [package="[THT]"]
  Rythm_2 = LED - 5mm [color="Green (570nm)" package="5 mm [THT]"]
  Mute_+_Beat = LED - 5mm [color="Red (633nm)" package="5 mm [THT]"]
  Audio_jack = Stereo Jack (TRS) 3.5mm [package="PG203J [THT]"]
  R7 = Resistor [tolerance=±5% resistance=100 package=THT]
  R8 = Resistor [tolerance=±5% resistance=100 package=THT]
  R9 = Resistor [tolerance=±5% resistance=100 package=THT]
  R10 = Resistor [tolerance=±5% resistance=100 package=THT]
  Arduino1 = Arduino

nets:
  N1: Freq_2.leg1, Decay_2.leg1, Freq_1.leg1, Decay_1.leg1, Freq.leg1, Beat_freq.leg1, Mute.Pin_4, Rythm.Pin_4, Arduino1.+5V
  N2: Freq_2.wiper, Arduino1.A4
  N3: Freq_2.leg2, Decay_2.leg2, Freq_1.leg2, Decay_1.leg2, Freq.leg2, Beat_freq.leg2, Audio_jack.Sleeve, R7.Pin_0, R8.Pin_0, R9.Pin_1, R10.Pin_1, Arduino1.GND
  N4: Decay_2.wiper, Arduino1.A3
  N5: Freq_1.wiper, Arduino1.A2
  N6: Decay_1.wiper, Arduino1.A1
  N7: Freq.wiper, Arduino1.A0
  N8: Beat_freq.wiper, Arduino1.A5
  N9: Mute.Pin_2, R10.Pin_0, Arduino1.D9
  N10: Rythm.Pin_2, R9.Pin_0, Arduino1.D10
  N11: Rythm_2.cathode, R7.Pin_1
  N12: Rythm_2.anode, Arduino1.D12
  N13: Mute_+_Beat.cathode, R8.Pin_1
  N14: Mute_+_Beat.anode, Arduino1.D6
  N15: Audio_jack.Ring, Arduino1.D11
  N16: Audio_jack.Tip, Arduino1.D3
